// Logisim project v5.circ as structural Verilog: 6 circuits, main circuit main
module main (
);

  wire clock_1_out, clock_2_out, clock_3_out, comparator_1_eq, comparator_2_eq, comparator_3_eq,
       comparator_4_eq, comparator_6_lt, comparator_7_gt, cpu_1_write_enable, priority_encoder_1_p3,
       priority_encoder_1_p4, priority_encoder_1_p5;
  wire [3:0] priority_encoder_1_p1;
  wire [6:0] keyboard_1_data;
  wire [7:0] cpu_1_data_out, multiplexer_1_out, numtostring_1_data_out, ram_1_dout, stringtonum_1_data_out;
  wire [7:7] undriven;
  wire [15:0] cpu_1_address;

  // Probe on cpu_1_address
  CPU cpu_1 (
    .DATA_IN(multiplexer_1_out), .WRITE_ENABLE(cpu_1_write_enable), .DATA_OUT(cpu_1_data_out),
    .ADDRESS(cpu_1_address));
  RAM #(.addrWidth(16), .enables("line")) ram_1 (
    .addr(cpu_1_address), .we(cpu_1_write_enable), .clk(clock_1_out), .din(cpu_1_data_out), .dout(ram_1_dout));
  Clock clock_1 (.out(clock_1_out));
  // Probe on multiplexer_1_out
  NumToString numtostring_1 (.DATA_IN(cpu_1_data_out), .Address(cpu_1_address), .DATA_OUT(numtostring_1_data_out));
  StringToNum stringtonum_1 (.DATA_IN(cpu_1_data_out), .ADDRESS(cpu_1_address), .DATA_OUT(stringtonum_1_data_out));
  Multiplexer #(.select(4), .width(8)) multiplexer_1 (
    .in0(ram_1_dout), .in1({undriven[7], keyboard_1_data}), .in2(numtostring_1_data_out),
    .in3(stringtonum_1_data_out), .out(multiplexer_1_out), .sel(priority_encoder_1_p1));  // open: in4, in5, in6, in7, in8, in9, in10, in11, in12, in13, in14, in15
  // Probe on priority_encoder_1_p1
  // Priority_Encoder #(.select(4)) priority_encoder_1: pin names not known; wires that end beside it: priority_encoder_1_p1, 1'b1, priority_encoder_1_p3, priority_encoder_1_p4, priority_encoder_1_p5
  Comparator #(.mode("unsigned"), .width(16)) comparator_1 (
    .a(cpu_1_address), .b(16'hff1d), .eq(comparator_1_eq));  // open: gt, lt
  Comparator #(.mode("unsigned"), .width(16)) comparator_2 (
    .a(cpu_1_address), .b(16'hff1e), .eq(comparator_2_eq));  // open: gt, lt
  Clock clock_2 (.out(clock_2_out));
  TTY #(.cols(64), .rows(16)) tty_1 (
    .data(cpu_1_data_out[6:0]), .clk(clock_2_out), .we(comparator_3_eq), .clr(comparator_4_eq));
  Comparator #(.width(16)) comparator_3 (.a(cpu_1_address), .b(16'hff02), .eq(comparator_3_eq));  // open: gt, lt
  Comparator #(.width(16)) comparator_4 (.a(cpu_1_address), .b(16'hff03), .eq(comparator_4_eq));  // open: gt, lt
  Comparator #(.width(16)) comparator_5 (.a(cpu_1_address), .b(16'hff04), .eq(priority_encoder_1_p3));  // open: gt, lt
  Comparator #(.mode("unsigned"), .width(16)) comparator_6 (
    .a(cpu_1_address), .b(16'hff1a), .lt(comparator_6_lt));  // open: gt, eq
  and and_1 (priority_encoder_1_p4, comparator_6_lt, comparator_7_gt);
  Comparator #(.mode("unsigned"), .width(16)) comparator_7 (
    .a(cpu_1_address), .b(16'hff11), .gt(comparator_7_gt));  // open: eq, lt
  or or_1 (priority_encoder_1_p5, comparator_1_eq, comparator_2_eq);
  Clock clock_3 (.out(clock_3_out));
  Keyboard #(.buflen(16)) keyboard_1 (
    .clk(clock_3_out), .re(priority_encoder_1_p3), .data(keyboard_1_data));  // open: clr, avail
endmodule

module CPU (
  input  [7:0] DATA_IN,
  output WRITE_ENABLE,
  output [7:0] DATA_OUT,
  output [15:0] ADDRESS
);

  wire and_1_out, clock_1_out, comparator_1_eq, comparator_2_eq, decoder_1_out1, decoder_1_out2,
       decoder_1_out3, decoder_1_out4, decoder_1_out5, decoder_1_out6, decoder_1_out7, decoder_1_out8,
       decoder_1_out9, decoder_1_out10, decoder_1_out11, decoder_1_out12, decoder_1_out13, decoder_1_out14,
       decoder_1_out15, DOUBLE_EXEC, or_2_out, or_3_out, or_4_out, PC_INCREMENT, SINGLE_EXEC;
  wire [3:0] ADDR_SEL, ARG0_q, ARG0_q_2, ARG1_q, ARG1_q_2, DEST, Opcode_q, Opcode_q_2, SRC;
  wire [7:0] A_q, and_2_out, B_q, CMP_q, FLAGS, FLAGS_q, multiplexer_2_out, pull_resistor_1_node,
       pull_resistor_2_node, pull_resistor_3_node;
  wire [15:0] adder_1_out, adder_2_out, ALU_OUT, bit_extender_1_out, D_q, DATA_BUS, DEST_DATA, IDX_q,
       multiplexer_3_out, multiplexer_6_out, multiplexer_7_out, multiplexer_8_out, PC_q, SP_q;
  wire [15:1] pull_resistor_4_node;

  Decoder #(.enable("false"), .select(4)) decoder_1 (
    .out1(decoder_1_out1), .out2(decoder_1_out2), .out3(decoder_1_out3), .out4(decoder_1_out4),
    .out5(decoder_1_out5), .out6(decoder_1_out6), .out7(decoder_1_out7), .out8(decoder_1_out8),
    .out9(decoder_1_out9), .out10(decoder_1_out10), .out11(decoder_1_out11), .out12(decoder_1_out12),
    .out13(decoder_1_out13), .out14(decoder_1_out14), .out15(decoder_1_out15), .sel(DEST));  // open: out0
  or or_1 (WRITE_ENABLE, decoder_1_out1, decoder_1_out2, decoder_1_out3, decoder_1_out4);
  Multiplexer #(.width(8)) multiplexer_1 (.in0(DATA_BUS[15:8]), .in1(DATA_BUS[7:0]), .out(DATA_OUT), .sel(or_4_out));
  Multiplexer #(.width(8)) multiplexer_2 (
    .in0(DATA_BUS[7:0]), .in1(DATA_BUS[15:8]), .out(multiplexer_2_out), .sel(decoder_1_out7));
  // Probe on DATA_BUS
  or or_2 (or_2_out, decoder_1_out7, decoder_1_out5);
  or or_3 (or_3_out, decoder_1_out6, decoder_1_out7);
  and and_1 (and_1_out, decoder_1_out9, comparator_1_eq);
  Register A (.D(multiplexer_2_out), .en(or_2_out), .Q(A_q), .clk(clock_1_out));  // open: clr
  Register B (.D(DATA_BUS[7:0]), .en(or_3_out), .Q(B_q), .clk(clock_1_out));  // open: clr
  Register #(.width(16)) D (.D(DATA_BUS), .en(decoder_1_out8), .Q(D_q), .clk(clock_1_out));  // open: clr
  Counter #(.max('hffff), .width(16)) PC (
    .load(and_1_out), .D(DATA_BUS), .count(PC_INCREMENT), .Q(PC_q), .clk(clock_1_out));  // open: carry, up, clr
  Register #(.width(16)) SP (.D(DATA_BUS), .en(decoder_1_out10), .Q(SP_q), .clk(clock_1_out));  // open: clr
  Register #(.width(16)) IDX (.D(DATA_BUS), .en(decoder_1_out11), .Q(IDX_q), .clk(clock_1_out));  // open: clr
  Register CMP (.D(DATA_BUS[7:0]), .en(decoder_1_out12), .Q(CMP_q), .clk(clock_1_out));  // open: clr
  Register u_FLAGS (.D(FLAGS), .en(comparator_2_eq), .Q(FLAGS_q), .clk(clock_1_out));  // open: clr
  Register Opcode (
    .D(DATA_BUS[7:0]), .en(decoder_1_out13), .Q({Opcode_q_2, Opcode_q}), .clk(clock_1_out));  // open: clr
  Register ARG0 (.D(DATA_BUS[7:0]), .en(decoder_1_out14), .Q({ARG0_q_2, ARG0_q}), .clk(clock_1_out));  // open: clr
  Register ARG1 (.D(DATA_BUS[7:0]), .en(decoder_1_out15), .Q({ARG1_q_2, ARG1_q}), .clk(clock_1_out));  // open: clr
  Clock clock_1 (.out(clock_1_out));
  assign and_2_out = CMP_q & FLAGS_q;  // AND_Gate and_2, 8 bits wide
  Pull_Resistor pull_resistor_1 (.node(pull_resistor_1_node));
  Pull_Resistor pull_resistor_2 (.node(pull_resistor_2_node));
  // Probe on {A_q, B_q}
  Comparator comparator_1 (.a(CMP_q), .b(and_2_out), .eq(comparator_1_eq));  // open: gt, lt
  Comparator #(.width(4)) comparator_2 (.a(Opcode_q_2), .b(4'b1100), .eq(comparator_2_eq));  // open: gt, lt
  Pull_Resistor pull_resistor_3 (.node(pull_resistor_3_node));
  Multiplexer #(.width(16)) multiplexer_3 (
    .in0({pull_resistor_1_node, DATA_IN}), .in1({DEST_DATA[7:0], DATA_IN}), .out(multiplexer_3_out),
    .sel(or_4_out));
  // Probe on multiplexer_3_out
  Multiplexer #(.select(4), .width(16)) multiplexer_4 (
    .in0({16{1'b0}}), .in1(multiplexer_3_out), .in2(multiplexer_3_out), .in3(multiplexer_3_out),
    .in4(multiplexer_3_out), .in5({pull_resistor_2_node, A_q}), .in6({pull_resistor_2_node, B_q}),
    .in7({A_q, B_q}), .in8(D_q), .in9(PC_q), .in10(SP_q), .in11(IDX_q), .in12(ALU_OUT),
    .in14({pull_resistor_3_node, ARG0_q_2, ARG0_q}), .in15({ARG0_q_2, ARG0_q, ARG1_q_2, ARG1_q}),
    .out(DATA_BUS), .sel(SRC));  // open: in13
  Multiplexer #(.select(4), .width(16)) multiplexer_5 (
    .in0({16{1'b0}}), .in1(multiplexer_3_out), .in2(multiplexer_3_out), .in3(multiplexer_3_out),
    .in4(multiplexer_3_out), .in5({pull_resistor_2_node, A_q}), .in6({pull_resistor_2_node, B_q}),
    .in7({A_q, B_q}), .in8(D_q), .in9(PC_q), .in10(SP_q), .in11(IDX_q), .in12(ALU_OUT),
    .in14({pull_resistor_3_node, ARG0_q_2, ARG0_q}), .in15({ARG0_q_2, ARG0_q, ARG1_q_2, ARG1_q}),
    .out(DEST_DATA), .sel(DEST));  // open: in13
  Adder #(.width(16)) adder_1 (
    .a(IDX_q), .b({ARG0_q_2, ARG0_q, ARG1_q_2, ARG1_q}), .out(adder_1_out));  // open: cin, cout
  Multiplexer #(.select(4), .width(16)) multiplexer_6 (
    .in0(bit_extender_1_out), .in1(multiplexer_3_out), .in2(multiplexer_3_out), .in3(multiplexer_3_out),
    .in4(multiplexer_3_out), .in5({pull_resistor_2_node, A_q}), .in6({pull_resistor_2_node, B_q}),
    .in7({A_q, B_q}), .in8(D_q), .in9(PC_q), .in10(SP_q), .in11(IDX_q), .in12(ALU_OUT),
    .in14({pull_resistor_3_node, ARG0_q_2, ARG0_q}), .in15({ARG0_q_2, ARG0_q, ARG1_q_2, ARG1_q}),
    .out(multiplexer_6_out), .sel(ARG0_q_2));  // open: in13
  Multiplexer #(.select(4), .width(16)) multiplexer_7 (
    .in0(bit_extender_1_out), .in1(multiplexer_3_out), .in2(multiplexer_3_out), .in3(multiplexer_3_out),
    .in4(multiplexer_3_out), .in5({pull_resistor_2_node, A_q}), .in6({pull_resistor_2_node, B_q}),
    .in7({A_q, B_q}), .in8(D_q), .in9(PC_q), .in10(SP_q), .in11(IDX_q), .in12(ALU_OUT),
    .in14({pull_resistor_3_node, ARG0_q_2, ARG0_q}), .in15({ARG0_q_2, ARG0_q, ARG1_q_2, ARG1_q}),
    .out(multiplexer_7_out), .sel(ARG0_q));  // open: in13
  or or_4 (or_4_out, DOUBLE_EXEC, SINGLE_EXEC);
  Adder #(.width(16)) adder_2 (
    .a(SP_q), .b({ARG0_q_2, ARG0_q, ARG1_q_2, ARG1_q}), .out(adder_2_out));  // open: cin, cout
  Multiplexer #(.select(4), .width(16)) multiplexer_8 (
    .in0({16{1'b0}}), .in1(multiplexer_3_out), .in2(multiplexer_3_out), .in3(multiplexer_3_out),
    .in4(ALU_OUT), .in5({pull_resistor_2_node, A_q}), .in6({pull_resistor_2_node, B_q}), .in7({A_q, B_q}),
    .in8(D_q), .in9(PC_q), .in10(adder_2_out), .in11(adder_1_out), .in12(ALU_OUT),
    .in14({pull_resistor_3_node, ARG0_q_2, ARG0_q}), .in15({ARG0_q_2, ARG0_q, ARG1_q_2, ARG1_q}),
    .out(multiplexer_8_out), .sel(ADDR_SEL));  // open: in13
  assign bit_extender_1_out = {{12{1'b0}}, ARG1_q};  // Bit_Extender bit_extender_1
  Pipeline pipeline_1 (
    .Opcode({Opcode_q_2, Opcode_q}), .DEST(DEST), .SRC(SRC), .ADDR_SEL(ADDR_SEL),
    .PC_INCREMENT(PC_INCREMENT), .DOUBLE_EXEC(DOUBLE_EXEC), .SINGLE_EXEC(SINGLE_EXEC));
  Pull_Resistor pull_resistor_4 (.node({pull_resistor_4_node, DOUBLE_EXEC}));
  Adder #(.width(16)) adder_3 (
    .a(multiplexer_8_out), .b({pull_resistor_4_node, DOUBLE_EXEC}), .out(ADDRESS));  // open: cin, cout
  ALU alu_1 (
    .ALU_TOP(multiplexer_6_out), .ALU_BOTTOM(multiplexer_7_out), .ALU_OP(ARG1_q_2), .ALU_OUT(ALU_OUT),
    .FLAGS(FLAGS));
endmodule

module Pipeline (
  input  [7:0] Opcode,
  output [3:0] DEST,
  output [3:0] SRC,
  output [3:0] ADDR_SEL,
  output PC_INCREMENT,
  output DOUBLE_EXEC,
  output SINGLE_EXEC
);

  wire and_1_out, clock_1_out, comparator_1_gt, comparator_2_lt, comparator_3_gt, comparator_4_gt,
       comparator_5_lt, comparator_7_eq, decoder_1_out0, decoder_1_out3, not_1_out;
  wire [2:0] counter_1_q, DEST_ARG_data, multiplexer_3_out, multiplexer_4_out, multiplexer_5_out, or_1_out,
       SRC_ARG_data;
  wire [3:0] multiplexer_1_out, multiplexer_2_out, rom_1_data;

  ROM #(.addrWidth(4), .dataWidth(3)) SRC_ARG (.addr(Opcode[7:4]), .data(SRC_ARG_data));
  ROM #(.addrWidth(4), .dataWidth(3)) DEST_ARG (.addr(Opcode[3:0]), .data(DEST_ARG_data));
  Comparator #(.mode("unsigned"), .width(4)) comparator_1 (
    .a(Opcode[7:4]), .b(Opcode[3:0]), .gt(comparator_1_gt));  // open: eq, lt
  Multiplexer #(.width(4)) multiplexer_1 (
    .in0(Opcode[3:0]), .in1(Opcode[7:4]), .out(multiplexer_1_out), .sel(comparator_1_gt));
  Multiplexer #(.width(4)) multiplexer_2 (
    .in0(Opcode[7:4]), .in1(Opcode[3:0]), .out(multiplexer_2_out), .sel(comparator_1_gt));
  Comparator #(.mode("unsigned"), .width(4)) comparator_2 (
    .a(multiplexer_1_out), .b(4'b1111), .lt(comparator_2_lt));  // open: gt, eq
  Comparator #(.mode("unsigned"), .width(4)) comparator_3 (
    .a(multiplexer_1_out), .b(4'b0110), .gt(comparator_3_gt));  // open: eq, lt
  Comparator #(.mode("unsigned"), .width(4)) comparator_4 (
    .a(4'b0101), .b(multiplexer_2_out), .gt(comparator_4_gt));  // open: eq, lt
  Comparator #(.mode("unsigned"), .width(4)) comparator_5 (
    .a(4'b0000), .b(multiplexer_2_out), .lt(comparator_5_lt));  // open: gt, eq
  ROM #(.addrWidth(4), .dataWidth(4)) rom_1 (.addr(multiplexer_2_out), .data(rom_1_data));
  assign or_1_out = SRC_ARG_data | DEST_ARG_data;  // OR_Gate or_1, 3 bits wide
  Multiplexer #(.width(3)) multiplexer_3 (.in0(3'b011), .in1(3'b100), .out(multiplexer_3_out), .sel(and_1_out));
  Decoder #(.enable("false"), .select(3)) decoder_1 (
    .out0(decoder_1_out0), .out3(decoder_1_out3), .sel(counter_1_q));  // open: out1, out2, out4, out5, out6, out7
  and and_1 (and_1_out, comparator_3_gt, comparator_2_lt, comparator_4_gt, comparator_5_lt);
  Multiplexer #(.select(3), .width(3)) multiplexer_4 (
    .in0(or_1_out), .in1(or_1_out), .in2(or_1_out), .in3(multiplexer_3_out), .in4(multiplexer_3_out),
    .out(multiplexer_4_out), .sel(counter_1_q));  // open: in5, in6, in7
  // OR_Gate or_2 has open pins: in0=decoder_1_out0, in1=decoder_1_out3, out=open
  Clock clock_1 (.out(clock_1_out));
  Multiplexer #(.select(3), .width(3)) multiplexer_5 (
    .in0(3'b011), .in1(3'b011), .in2(3'b011), .in3(3'b000), .in4(3'b000), .out(multiplexer_5_out),
    .sel(counter_1_q));  // open: in5, in6, in7
  // Probe on multiplexer_5_out
  Counter #(.max('h4), .width(3)) counter_1 (
    .load(comparator_7_eq), .D(multiplexer_5_out), .Q(counter_1_q), .clk(not_1_out));  // open: count, carry, up, clr
  not not_1 (not_1_out, clock_1_out);
  Comparator #(.mode("unsigned"), .width(3)) comparator_6 ();  // open: a, b, gt, eq, lt
  Comparator #(.mode("unsigned"), .width(3)) comparator_7 (
    .a(multiplexer_4_out), .b(counter_1_q), .eq(comparator_7_eq));  // open: gt, lt
  Multiplexer #(.select(3), .width(8)) multiplexer_6 (
    .in0(8'h4d), .in1(8'h4e), .in2(8'h4f), .in3(Opcode), .in4(Opcode), .out({SRC, DEST}), .sel(counter_1_q));  // open: in5, in6, in7
  Multiplexer #(.select(3), .width(4)) multiplexer_7 (
    .in0(4'b1001), .in1(4'b1001), .in2(4'b1001), .in3(rom_1_data), .in4(rom_1_data), .out(ADDR_SEL),
    .sel(counter_1_q));  // open: in5, in6, in7
  Comparator #(.mode("unsigned"), .width(3)) comparator_8 (
    .a(counter_1_q), .b(3'b011), .lt(PC_INCREMENT));  // open: gt, eq
  Comparator #(.mode("unsigned"), .width(3)) comparator_9 (
    .a(counter_1_q), .b(3'b100), .eq(DOUBLE_EXEC));  // open: gt, lt
  not not_2 (SINGLE_EXEC, and_1_out);

  // Notes on the sheet:
  //   contents of SRC_ARG (hex, n*v repeats v):
  //   0 4*2 7*0 2 0 1 2
  //   contents of DEST_ARG (hex, n*v repeats v):
  //   0 4*2
  //   contents of rom_1 (hex, n*v repeats v):
  //   0 f a b 4
endmodule

module ALU (
  input  [15:0] ALU_TOP,
  input  [15:0] ALU_BOTTOM,
  input  [3:0] ALU_OP,
  output [15:0] ALU_OUT,
  output [7:0] FLAGS
);

  wire adder_1_cout, pull_resistor_5_node, pull_resistor_6_node, subtractor_1_bout;
  wire [14:0] pull_resistor_1_node, pull_resistor_2_node, pull_resistor_3_node, pull_resistor_4_node;
  wire [15:0] adder_1_out, and_1_out, divider_1_out, divider_1_rem, divider_2_out, multiplier_1_out,
       multiplier_2_out, not_1_out, or_1_out, subtractor_1_out, xor_1_out;

  assign and_1_out = ALU_TOP & ALU_BOTTOM;  // AND_Gate and_1, 16 bits wide
  assign or_1_out = ALU_TOP | ALU_BOTTOM;  // OR_Gate or_1, 16 bits wide
  assign xor_1_out = ALU_TOP ^ ALU_BOTTOM;  // XOR_Gate xor_1, 16 bits wide
  Adder #(.width(16)) adder_1 (.a(ALU_TOP), .b(ALU_BOTTOM), .out(adder_1_out), .cout(adder_1_cout));  // open: cin
  Subtractor #(.width(16)) subtractor_1 (
    .a(ALU_TOP), .b(ALU_BOTTOM), .out(subtractor_1_out), .bout(subtractor_1_bout));  // open: bin
  Multiplier #(.width(16)) multiplier_1 (.a(ALU_TOP), .b(ALU_BOTTOM), .out(multiplier_1_out));  // open: cin, cout
  Multiplier #(.mode("twosComplement"), .width(16)) multiplier_2 (
    .a(ALU_TOP), .b(ALU_BOTTOM), .out(multiplier_2_out));  // open: cin, cout
  Divider #(.width(16)) divider_1 (
    .a(ALU_TOP), .b(ALU_BOTTOM), .out(divider_1_out), .rem(divider_1_rem));  // open: upper
  Divider #(.mode("twosComplement"), .width(16)) divider_2 (
    .a(ALU_TOP), .b(ALU_BOTTOM), .out(divider_2_out));  // open: upper, rem
  assign not_1_out = ~ALU_TOP;  // NOT_Gate not_1, 16 bits wide
  Comparator #(.width(16)) comparator_1 (.a(ALU_TOP), .b(ALU_BOTTOM), .gt(FLAGS[1]), .eq(FLAGS[0]), .lt(FLAGS[2]));
  or or_2 (FLAGS[7], FLAGS[1], FLAGS[0]);
  Pull_Resistor pull_resistor_1 (.node(pull_resistor_1_node));
  Pull_Resistor pull_resistor_2 (.node(pull_resistor_2_node));
  Pull_Resistor pull_resistor_3 (.node(pull_resistor_3_node));
  not not_2 (FLAGS[3], FLAGS[0]);
  or or_3 (FLAGS[6], FLAGS[0], FLAGS[2]);
  Pull_Resistor pull_resistor_4 (.node(pull_resistor_4_node));
  Pull_Resistor pull_resistor_5 (.node(pull_resistor_5_node));
  Pull_Resistor pull_resistor_6 (.node(pull_resistor_6_node));
  Multiplexer #(.select(4)) multiplexer_1 (
    .in0(pull_resistor_5_node), .in1(pull_resistor_5_node), .in2(pull_resistor_5_node), .in3(adder_1_cout),
    .in4(subtractor_1_bout), .in5(pull_resistor_6_node), .in6(pull_resistor_6_node),
    .in7(pull_resistor_6_node), .in8(pull_resistor_6_node), .in9(pull_resistor_6_node),
    .in10(pull_resistor_6_node), .in11(pull_resistor_6_node), .in12(pull_resistor_6_node),
    .in13(pull_resistor_6_node), .in14(pull_resistor_6_node), .in15(pull_resistor_6_node), .out(FLAGS[5]),
    .sel(ALU_OP));
  Multiplexer #(.select(4), .width(16)) multiplexer_2 (
    .in0(and_1_out), .in1(or_1_out), .in2(xor_1_out), .in3(adder_1_out), .in4(subtractor_1_out),
    .in5(multiplier_1_out), .in6(multiplier_2_out), .in7(divider_1_out), .in8(divider_2_out),
    .in9(divider_1_rem), .in10(not_1_out), .in11({pull_resistor_4_node, FLAGS[3]}),
    .in12({pull_resistor_1_node, FLAGS[0]}), .in13({pull_resistor_2_node, FLAGS[1]}),
    .in14({pull_resistor_3_node, FLAGS[2]}), .out(ALU_OUT), .sel(ALU_OP));  // open: in15
  Comparator #(.mode("unsigned"), .width(16)) comparator_2 (
    .a(ALU_OUT), .b({16{1'b0}}), .eq(FLAGS[4]));  // open: gt, lt
  Pull_Resistor pull_resistor_7 (.node(FLAGS[4]));
endmodule

module NumToString (
  input  [7:0] DATA_IN,
  input  [15:0] Address,
  output [7:0] DATA_OUT
);

  wire and_1_out, and_2_out, and_3_out, and_4_out, clock_1_out, comparator_1_eq, comparator_2_eq,
       comparator_3_eq, comparator_4_eq, comparator_5_eq, comparator_6_eq, decoder_1_out0, decoder_1_out1,
       decoder_1_out2;
  wire [2:0] priority_encoder_1_out;
  wire [7:0] adder_1_out, adder_2_out, adder_3_out, adder_4_out, adder_5_out, BOTTOM_q, multiplexer_1_out,
       multiplexer_2_out, multiplexer_3_out, multiplexer_4_out, multiplexer_5_out, shift_register_1_out,
       shift_register_1_q0, shift_register_1_q1, shift_register_1_q2, shift_register_1_q3,
       shift_register_1_q4, shift_register_1_q5, shift_register_1_q6, TOP_q;
  wire [15:0] divider_1_out, divider_1_rem, divider_2_out, divider_2_rem, divider_3_out, divider_3_rem,
       divider_4_out, divider_4_rem, divider_5_rem;

  Decoder #(.select(4)) decoder_1 (
    .out0(decoder_1_out0), .out1(decoder_1_out1), .out2(decoder_1_out2), .sel(Address[3:0]),
    .en(comparator_1_eq));  // open: out3, out4, out5, out6, out7, out8, out9, out10, out11, out12, out13, out14, out15
  Comparator #(.width(12)) comparator_1 (.a(Address[15:4]), .b(12'hff1), .eq(comparator_1_eq));  // open: gt, lt
  Clock clock_1 (.out(clock_1_out));
  // Probe on {TOP_q, BOTTOM_q}
  Register TOP (.D(DATA_IN), .en(decoder_1_out0), .Q(TOP_q), .clk(clock_1_out));  // open: clr
  Register BOTTOM (.D(DATA_IN), .en(decoder_1_out1), .Q(BOTTOM_q), .clk(clock_1_out));  // open: clr
  Divider #(.width(16)) divider_1 (
    .a({TOP_q, BOTTOM_q}), .b(16'ha), .out(divider_1_out), .rem(divider_1_rem));  // open: upper
  Divider #(.width(16)) divider_2 (
    .a(divider_1_out), .b(16'ha), .out(divider_2_out), .rem(divider_2_rem));  // open: upper
  Adder adder_1 (.a(divider_1_rem[7:0]), .b(8'h30), .out(adder_1_out));  // open: cin, cout
  Divider #(.width(16)) divider_3 (
    .a(divider_2_out), .b(16'ha), .out(divider_3_out), .rem(divider_3_rem));  // open: upper
  Adder adder_2 (.a(divider_2_rem[7:0]), .b(8'h30), .out(adder_2_out));  // open: cin, cout
  Comparator comparator_2 (.a(adder_1_out), .b(8'h30), .eq(comparator_2_eq));  // open: gt, lt
  Multiplexer #(.select(3), .width(8)) multiplexer_1 (
    .in0(adder_1_out), .in1({8{1'b0}}), .in2({8{1'b0}}), .in3({8{1'b0}}), .in4({8{1'b0}}), .in5({8{1'b0}}),
    .in6({8{1'b0}}), .in7({8{1'b0}}), .out(multiplexer_1_out), .sel(priority_encoder_1_out));
  Adder adder_3 (.a(divider_3_rem[7:0]), .b(8'h30), .out(adder_3_out));  // open: cin, cout
  Comparator comparator_3 (.a(adder_2_out), .b(8'h30), .eq(comparator_3_eq));  // open: gt, lt
  Multiplexer #(.select(3), .width(8)) multiplexer_2 (
    .in0(adder_2_out), .in1(adder_1_out), .in2({8{1'b0}}), .in3({8{1'b0}}), .in4({8{1'b0}}), .in5({8{1'b0}}),
    .in6({8{1'b0}}), .in7({8{1'b0}}), .out(multiplexer_2_out), .sel(priority_encoder_1_out));
  Divider #(.width(16)) divider_4 (
    .a(divider_3_out), .b(16'ha), .out(divider_4_out), .rem(divider_4_rem));  // open: upper
  Adder adder_4 (.a(divider_4_rem[7:0]), .b(8'h30), .out(adder_4_out));  // open: cin, cout
  Comparator comparator_4 (.a(adder_3_out), .b(8'h30), .eq(comparator_4_eq));  // open: gt, lt
  Multiplexer #(.select(3), .width(8)) multiplexer_3 (
    .in0(adder_3_out), .in1(adder_2_out), .in2(adder_1_out), .in3({8{1'b0}}), .in4({8{1'b0}}),
    .in5({8{1'b0}}), .in6({8{1'b0}}), .in7({8{1'b0}}), .out(multiplexer_3_out), .sel(priority_encoder_1_out));
  Divider #(.width(16)) divider_5 (.a(divider_4_out), .b(16'ha), .rem(divider_5_rem));  // open: out, upper
  Adder adder_5 (.a(divider_5_rem[7:0]), .b(8'h30), .out(adder_5_out));  // open: cin, cout
  Comparator comparator_5 (.a(adder_4_out), .b(8'h30), .eq(comparator_5_eq));  // open: gt, lt
  Multiplexer #(.select(3), .width(8)) multiplexer_4 (
    .in0(adder_4_out), .in1(adder_3_out), .in2(adder_2_out), .in3(adder_1_out), .in4({8{1'b0}}),
    .in5({8{1'b0}}), .in6({8{1'b0}}), .in7({8{1'b0}}), .out(multiplexer_4_out), .sel(priority_encoder_1_out));
  Shift_Register #(.trigger("falling"), .width(8)) shift_register_1 (
    .shift(decoder_1_out2), .clk(clock_1_out), .out(shift_register_1_out), .load(decoder_1_out1),
    .d0({8{1'b0}}), .q0(shift_register_1_q0), .d1({8{1'b0}}), .q1(shift_register_1_q1), .d2({8{1'b0}}),
    .q2(shift_register_1_q2), .d3(multiplexer_1_out), .q3(shift_register_1_q3), .d4(multiplexer_2_out),
    .q4(shift_register_1_q4), .d5(multiplexer_3_out), .q5(shift_register_1_q5), .d6(multiplexer_4_out),
    .q6(shift_register_1_q6), .d7(multiplexer_5_out));  // open: in, clr, q7
  Comparator comparator_6 (.a(adder_5_out), .b(8'h30), .eq(comparator_6_eq));  // open: gt, lt
  Multiplexer #(.select(3), .width(8)) multiplexer_5 (
    .in0(adder_5_out), .in1(adder_4_out), .in2(adder_3_out), .in3(adder_2_out), .in4(adder_1_out),
    .in5(adder_1_out), .in6({8{1'b0}}), .in7({8{1'b0}}), .out(multiplexer_5_out), .sel(priority_encoder_1_out));
  // Probe on shift_register_1_out
  // Probe on shift_register_1_q6
  // Probe on shift_register_1_q5
  // Probe on shift_register_1_q4
  // Probe on shift_register_1_q2
  and and_1 (and_1_out, comparator_6_eq, comparator_5_eq);
  and and_2 (and_2_out, and_1_out, comparator_4_eq);
  and and_3 (and_3_out, and_2_out, comparator_3_eq);
  and and_4 (and_4_out, and_3_out, comparator_2_eq);
  Multiplexer #(.enable("true"), .select(4), .width(8)) multiplexer_6 (
    .in2(shift_register_1_out), .in3(shift_register_1_out), .in4(shift_register_1_out),
    .in5(shift_register_1_q6), .in6(shift_register_1_q5), .in7(shift_register_1_q4),
    .in8(shift_register_1_q3), .in9(shift_register_1_q2), .in10(shift_register_1_q1),
    .in11(shift_register_1_q0), .out(DATA_OUT), .sel(Address[3:0]), .en(comparator_1_eq));  // open: in0, in1, in12, in13, in14, in15
  Priority_Encoder priority_encoder_1 (
    .in0(1'b1), .in1(comparator_6_eq), .in2(and_1_out), .in3(and_2_out), .in4(and_3_out), .in5(and_4_out),
    .out(priority_encoder_1_out));  // open: in6, in7, en_in, gs, en_out
endmodule

module StringToNum (
  input  [7:0] DATA_IN,
  input  [15:0] ADDRESS,
  output [7:0] DATA_OUT
);

  wire and_1_out, clock_1_out, comparator_1_lt, comparator_2_gt, comparator_3_eq, comparator_4_eq,
       comparator_5_eq;
  wire [7:0] adder_4_out, adder_4_out_2, shift_register_1_out, shift_register_1_q0, shift_register_1_q1,
       shift_register_1_q2, shift_register_1_q3, subtractor_1_out;
  wire [15:0] adder_1_out, adder_2_out, adder_3_out, multiplier_1_out, multiplier_2_out, multiplier_3_out,
       multiplier_4_out;
  wire [15:8] pull_resistor_1_node, pull_resistor_2_node, pull_resistor_3_node, pull_resistor_4_node,
       pull_resistor_5_node;

  Comparator #(.mode("unsigned")) comparator_1 (.a(DATA_IN), .b(8'h3a), .lt(comparator_1_lt));  // open: gt, eq
  Comparator #(.mode("unsigned")) comparator_2 (.a(DATA_IN), .b(8'h2f), .gt(comparator_2_gt));  // open: eq, lt
  Subtractor subtractor_1 (.a(DATA_IN), .b(8'h30), .out(subtractor_1_out));  // open: bin, bout
  Comparator #(.mode("unsigned"), .width(16)) comparator_3 (
    .a(ADDRESS), .b(16'hff1b), .eq(comparator_3_eq));  // open: gt, lt
  Comparator #(.mode("unsigned"), .width(16)) comparator_4 (
    .a(ADDRESS), .b(16'hff1c), .eq(comparator_4_eq));  // open: gt, lt
  and and_1 (and_1_out, comparator_1_lt, comparator_3_eq, comparator_2_gt);
  Clock clock_1 (.out(clock_1_out));
  Shift_Register #(.length(5), .width(8)) shift_register_1 (
    .shift(and_1_out), .in(subtractor_1_out), .clk(clock_1_out), .out(shift_register_1_out),
    .clr(comparator_4_eq), .q0(shift_register_1_q0), .q1(shift_register_1_q1), .q2(shift_register_1_q2),
    .q3(shift_register_1_q3));  // open: load, d0, d1, d2, d3, d4, q4
  Pull_Resistor pull_resistor_1 (.node({pull_resistor_1_node, shift_register_1_out}));
  Multiplier #(.width(16)) multiplier_1 (
    .a(16'h2710), .b({pull_resistor_1_node, shift_register_1_out}), .out(multiplier_1_out));  // open: cin, cout
  Pull_Resistor pull_resistor_2 (.node({pull_resistor_2_node, shift_register_1_q3}));
  Multiplier #(.width(16)) multiplier_2 (
    .a(16'h3e8), .b({pull_resistor_2_node, shift_register_1_q3}), .out(multiplier_2_out));  // open: cin, cout
  Pull_Resistor pull_resistor_3 (.node({pull_resistor_3_node, shift_register_1_q2}));
  Adder #(.width(16)) adder_1 (.a(multiplier_1_out), .b(multiplier_2_out), .out(adder_1_out));  // open: cin, cout
  Multiplier #(.width(16)) multiplier_3 (
    .a(16'h64), .b({pull_resistor_3_node, shift_register_1_q2}), .out(multiplier_3_out));  // open: cin, cout
  Pull_Resistor pull_resistor_4 (.node({pull_resistor_4_node, shift_register_1_q1}));
  Adder #(.width(16)) adder_2 (.a(adder_1_out), .b(multiplier_3_out), .out(adder_2_out));  // open: cin, cout
  Multiplier #(.width(16)) multiplier_4 (
    .a(16'ha), .b({pull_resistor_4_node, shift_register_1_q1}), .out(multiplier_4_out));  // open: cin, cout
  Pull_Resistor pull_resistor_5 (.node({pull_resistor_5_node, shift_register_1_q0}));
  Adder #(.width(16)) adder_3 (.a(adder_2_out), .b(multiplier_4_out), .out(adder_3_out));  // open: cin, cout
  Comparator #(.mode("unsigned"), .width(16)) comparator_5 (
    .a(ADDRESS), .b(16'hff1e), .eq(comparator_5_eq));  // open: gt, lt
  // Probe on {adder_4_out_2, adder_4_out}
  Adder #(.width(16)) adder_4 (
    .a(adder_3_out), .b({pull_resistor_5_node, shift_register_1_q0}), .out({adder_4_out_2, adder_4_out}));  // open: cin, cout
  Multiplexer #(.width(8)) multiplexer_1 (
    .in0(adder_4_out_2), .in1(adder_4_out), .out(DATA_OUT), .sel(comparator_5_eq));
endmodule
